// Logisim project EXP3.circ as structural Verilog: 1 circuit, main circuit main
module main (
  input  B,
  input  A,
  input  B_2,
  input  A_2,
  input  in_5,
  input  in_6,
  input  B_3,
  input  A_3,
  input  B_4,
  input  A_4,
  output out_11,
  output out_12,
  output out_13,
  output out_14,
  output out_15,
  output out_16,
  output out_17,
  output out_18
);

  wire n7400_1_p3, n7400_2_p3, n7400_2_p4, n7400_3_p3, n7400_3_p6, n7400_3_p7, n7400_4_p3, n7400_4_p6,
       n7400_4_p7, n7402_1_p1, n7402_1_p4, n7402_2_p1, n7402_3_p1, n7402_3_p4, n7402_3_p8, n7402_4_p3,
       n7402_4_p6, n7402_4_p9, n7402_4_p11;

  // _7400 7400_1: pin names not known; wires that end beside it: A_2, B_2, n7400_1_p3, n7400_1_p3, n7400_1_p3, out_11
  // _7400 7400_2: pin names not known; wires that end beside it: B_4, A_4, n7400_2_p3, n7400_2_p4, A_4, A_4, n7400_2_p3, B_4, B_4, n7400_2_p4, n7400_2_p3, n7400_2_p4, out_14
  // _7400 7400_3: pin names not known; wires that end beside it: in_5, in_5, n7400_3_p3, in_6, in_6, n7400_3_p6, n7400_3_p7, n7400_3_p7, out_12, n7400_3_p6, n7400_3_p3, n7400_3_p7
  // _7400 7400_4: pin names not known; wires that end beside it: A_3, B_3, n7400_4_p3, n7400_4_p3, A_3, n7400_4_p6, n7400_4_p7, n7400_4_p6, out_15, B_3, n7400_4_p3, n7400_4_p7
  // _7402 7402_1: pin names not known; wires that end beside it: n7402_1_p1, A, A, n7402_1_p4, B, B, out_13, n7402_1_p1, n7402_1_p4
  // _7402 7402_2: pin names not known; wires that end beside it: n7402_2_p1, A, B, out_16, n7402_2_p1, n7402_2_p1
  // _7402 7402_3: pin names not known; wires that end beside it: n7402_3_p1, A, A, n7402_3_p4, B, B, out_17, n7402_3_p8, n7402_3_p8, n7402_3_p8, n7402_3_p4, n7402_3_p1
  // _7402 7402_4: pin names not known; wires that end beside it: B, A, n7402_4_p3, A, B, n7402_4_p6, n7402_4_p3, A, n7402_4_p9, n7402_4_p6, n7402_4_p11, n7402_4_p11, B, n7402_4_p3
  // _7402 7402_5: pin names not known; wires that end beside it: out_18, n7402_4_p9, n7402_4_p9

  // Notes on the sheet:
  //   NAND TO AND
  //   NAND TO OR
  //   NAND TO NOR
  //   NAND TO XOR
  //   NOR TO AND
  //   NOR TO OR
  //   NOR TO NAND
  //   NOR TO XOR
endmodule
